// Logisim project processador.circ as structural Verilog: 10 circuits, main circuit controle
module controle (
  input  [15:0] \Instrução_Entrada ,
  output beq,
  output [12:0] \Instrução_Saída ,
  output sgt,
  output sw,
  output li,
  output add,
  output lw,
  output j,
  output [2:0] tipo_instr
);

  Decoder #(.select(3)) decoder_1 (
    .out0(lw), .out1(li), .out2(sgt), .out3(beq), .out4(sw), .out5(add), .out6(j),
    .sel(\Instrução_Entrada [15:13]), .en(1'b1));  // open: out7

  assign \Instrução_Saída  = \Instrução_Entrada [12:0];
  assign tipo_instr = \Instrução_Entrada [15:13];
endmodule

module PC (
  input  Clock,
  output [4:0] \Saída 
);

  wire [4:0] adder_1_out;

  Register #(.width(5)) register_1 (.D(adder_1_out), .Q(\Saída ), .clk(Clock));  // open: en, clr
  Adder #(.width(5)) adder_1 (.a(5'b00001), .b(\Saída ), .out(adder_1_out));  // open: cin, cout
endmodule

module li (
  input  [12:0] \Instrução ,
  input  Ativo,
  output [15:0] Imediato,
  output [2:0] Reg_dest
);

  assign Imediato = {{6{1'b0}}, \Instrução [9:0]};  // Bit_Extender bit_extender_1

  assign Reg_dest = \Instrução [12:10];
endmodule

module main (
  input  in_1,
  input  in_2,
  input  in_3,
  input  in_4,
  input  in_5,
  input  in_6,
  input  in_7,
  input  in_8,
  input  in_9,
  input  in_10,
  input  in_11,
  input  in_12,
  input  in_13,
  input  in_14,
  input  in_15,
  input  in_16,
  output [15:0] out_17,
  output [2:0] out_18
);

  wire clock_1_out, controle_1_add, controle_1_li, controle_1_lw, controle_1_sgt, escr_reg_ctrl_1_escr__la,
       escr_reg_ctrl_1_escr__t1, escr_reg_ctrl_1_escr__t2, escr_reg_ctrl_1_escr__t3;
  wire [2:0] add_1_reg_dest, inst, ler_add1, ler_add2, ler_lw, ler_reg_ctrl_1_reg_ler,
       ler_reg_ctrl_2_reg_ler, ler_sgt1, ler_sgt2, li_1_reg_dest, lw_1_reg_dest, sgt_1_reg_dest;
  wire [4:0] \pc_1_saída ;
  wire [12:0] instr_saida;
  wire [15:0] \add_1_saída , demultiplexer_1_out2, demultiplexer_1_out3, demultiplexer_1_out4,
       demultiplexer_1_out5, la_q, li_1_imediato, multiplexer_1_out, one_q, reg_ent_1, reg_ent_2,
       \sgt_1_saída , t1_q, t2_q, t3_q, zero_q;

  PC pc_1 (.Clock(clock_1_out), .\Saída (\pc_1_saída ));
  Clock clock_1 (.out(clock_1_out));
  controle controle_1 (
    .tipo_instr(inst), .lw(controle_1_lw), .li(controle_1_li), .sgt(controle_1_sgt), .add(controle_1_add),
    .\Instrução_Saída (instr_saida),
    .\Instrução_Entrada ({in_1, in_2, in_3, in_4, in_5, in_6, in_7, in_8, in_9, in_10, in_11, in_12, in_13, in_14, in_15, in_16}));  // open: beq, sw, j
  RAM #(.addrWidth(5), .dataWidth(16), .bus("separate")) ram_1 (
    .addr(\pc_1_saída ), .data(out_17));  // open: din, str, sel, clk, ld, clr
  li li_1 (.Reg_dest(li_1_reg_dest), .Imediato(li_1_imediato), .Ativo(controle_1_li), .\Instrução (instr_saida));
  Multiplexer #(.select(3), .width(16)) multiplexer_1 (
    .in1(li_1_imediato), .in2(\sgt_1_saída ), .in5(\add_1_saída ), .out(multiplexer_1_out), .sel(inst));  // open: in0, in3, in4, in6, in7, en
  lw lw_1 (.Reg_dest(lw_1_reg_dest), .Reg_ender(ler_lw), .\instrução (instr_saida));
  escr_reg_ctrl escr_reg_ctrl_1 (
    .lw(controle_1_lw), .reg_dest_lw(lw_1_reg_dest), .li(controle_1_li), .reg_dest_li(li_1_reg_dest),
    .sgt(controle_1_sgt), .reg_dest_sgt(sgt_1_reg_dest), .add(controle_1_add), .reg_dest_add(add_1_reg_dest),
    .tipo_instr(inst), .reg_dest(out_18), .escr__t1(escr_reg_ctrl_1_escr__t1),
    .escr__t2(escr_reg_ctrl_1_escr__t2), .escr__t3(escr_reg_ctrl_1_escr__t3),
    .escr__la(escr_reg_ctrl_1_escr__la));
  Demultiplexer #(.select(3), .width(16)) demultiplexer_1 (
    .out2(demultiplexer_1_out2), .out3(demultiplexer_1_out3), .out4(demultiplexer_1_out4),
    .out5(demultiplexer_1_out5), .in(multiplexer_1_out), .sel(out_18));  // open: out0, out1, out6, out7, en
  add add_1 (
    .Reg_dest(add_1_reg_dest), .Reg_1(ler_add1), .Reg_2(ler_add2), .reg_entr1(reg_ent_1),
    .reg_entr2(reg_ent_2), .\instrução (instr_saida), .\saída (\add_1_saída ));
  Register #(.width(16)) zero (.D({16{1'b0}}), .Q(zero_q), .clk(clock_1_out));  // open: en, clr
  Register #(.width(16)) one (.D(16'h1), .Q(one_q), .clk(clock_1_out));  // open: en, clr
  Register #(.width(16)) t1 (
    .D(demultiplexer_1_out2), .en(escr_reg_ctrl_1_escr__t1), .Q(t1_q), .clk(clock_1_out));  // open: clr
  Register #(.width(16)) t2 (
    .D(demultiplexer_1_out3), .en(escr_reg_ctrl_1_escr__t2), .Q(t2_q), .clk(clock_1_out));  // open: clr
  Register #(.width(16)) t3 (
    .D(demultiplexer_1_out4), .en(escr_reg_ctrl_1_escr__t3), .Q(t3_q), .clk(clock_1_out));  // open: clr
  Register #(.width(16)) la (
    .D(demultiplexer_1_out5), .en(escr_reg_ctrl_1_escr__la), .Q(la_q), .clr(clock_1_out));  // open: clk
  sgt sgt_1 (
    .Reg_dest(sgt_1_reg_dest), .Reg_1(ler_sgt1), .Reg_2(ler_sgt2), .reg_entr1(reg_ent_1),
    .reg_entr2(reg_ent_2), .\instrução (instr_saida), .\saída (\sgt_1_saída ));
  Multiplexer #(.select(3), .width(16)) multiplexer_2 (
    .in0(zero_q), .in1(one_q), .in2(t1_q), .in3(t2_q), .in4(t3_q), .in5(la_q), .out(reg_ent_1),
    .sel(ler_reg_ctrl_1_reg_ler));  // open: in6, in7, en
  Multiplexer #(.select(3), .width(16)) multiplexer_3 (
    .in0(zero_q), .in1(one_q), .in2(t1_q), .in3(t2_q), .in4(t3_q), .in5(la_q), .out(reg_ent_2),
    .sel(ler_reg_ctrl_2_reg_ler));  // open: in6, in7, en
  ler_reg_ctrl ler_reg_ctrl_1 (
    .ler_reg_lw(ler_lw), .ler_reg_sgt(ler_sgt1), .ler_reg_add(ler_add1), .tipo_instr(inst),
    .reg_ler(ler_reg_ctrl_1_reg_ler));  // open: ler_reg_beq, ler_reg_sw
  ler_reg_ctrl ler_reg_ctrl_2 (
    .ler_reg_lw(ler_lw), .ler_reg_sgt(ler_sgt2), .ler_reg_add(ler_add2), .tipo_instr(inst),
    .reg_ler(ler_reg_ctrl_2_reg_ler));  // open: ler_reg_beq, ler_reg_sw
  RAM #(.addrWidth(16), .dataWidth(16), .bus("separate")) ram_2 ();  // open: addr, din, data, str, sel, clk, ld, clr
endmodule

module escr_reg_ctrl (
  input  lw,
  input  [2:0] reg_dest_lw,
  input  li,
  input  [2:0] reg_dest_li,
  input  sgt,
  input  [2:0] reg_dest_sgt,
  input  add,
  input  [2:0] reg_dest_add,
  input  [2:0] tipo_instr,
  output [2:0] reg_dest,
  output escr__t1,
  output escr__t2,
  output escr__t3,
  output escr__la
);

  wire demultiplexer_1_out2, demultiplexer_1_out3, demultiplexer_1_out4, demultiplexer_1_out5, or_1_out;

  Multiplexer #(.select(3), .width(3)) multiplexer_1 (
    .in0(reg_dest_lw), .in1(reg_dest_li), .in2(reg_dest_sgt), .in3(3'b000), .in4(3'b000), .in5(reg_dest_add),
    .in6(3'b000), .in7(3'b000), .out(reg_dest), .sel(tipo_instr));  // open: en
  Demultiplexer #(.select(3)) demultiplexer_1 (
    .out2(demultiplexer_1_out2), .out3(demultiplexer_1_out3), .out4(demultiplexer_1_out4),
    .out5(demultiplexer_1_out5), .in(1'b1), .sel(reg_dest));  // open: out0, out1, out6, out7, en
  or or_1 (or_1_out, lw, li, sgt, add);
  and and_1 (escr__t1, or_1_out, demultiplexer_1_out2);
  and and_2 (escr__t2, or_1_out, demultiplexer_1_out3);
  and and_3 (escr__t3, or_1_out, demultiplexer_1_out4);
  and and_4 (escr__la, or_1_out, demultiplexer_1_out5);
endmodule

module add (
  input  [15:0] reg_entr1,
  input  [15:0] reg_entr2,
  input  [12:0] \instrução ,
  output [15:0] \saída ,
  output [2:0] Reg_1,
  output [2:0] Reg_2,
  output [2:0] Reg_dest
);

  Adder #(.width(16)) adder_1 (.a(reg_entr1), .b(reg_entr2), .out(\saída ));  // open: cin, cout

  assign Reg_1 = \instrução [9:7];
  assign Reg_2 = \instrução [6:4];
  assign Reg_dest = \instrução [12:10];
endmodule

module sgt (
  input  [15:0] reg_entr1,
  input  [15:0] reg_entr2,
  input  [12:0] \instrução ,
  output [15:0] \saída ,
  output [2:0] Reg_1,
  output [2:0] Reg_2,
  output [2:0] Reg_dest
);

  wire comparator_1_gt;

  Comparator #(.width(16)) comparator_1 (.a(reg_entr1), .b(reg_entr2), .gt(comparator_1_gt));  // open: eq, lt
  assign \saída  = {{15{1'b0}}, comparator_1_gt};  // Bit_Extender bit_extender_1

  assign Reg_1 = \instrução [9:7];
  assign Reg_2 = \instrução [6:4];
  assign Reg_dest = \instrução [12:10];
endmodule

module ler_reg_ctrl (
  input  [2:0] ler_reg_lw,
  input  [2:0] ler_reg_sgt,
  input  [2:0] ler_reg_beq,
  input  [2:0] ler_reg_sw,
  input  [2:0] ler_reg_add,
  input  [2:0] tipo_instr,
  output [2:0] reg_ler
);

  Multiplexer #(.select(3), .width(3)) multiplexer_1 (
    .in0(ler_reg_lw), .in1(3'b000), .in2(ler_reg_sgt), .in3(ler_reg_beq), .in4(ler_reg_sw),
    .in5(ler_reg_add), .in6(3'b000), .in7(3'b000), .out(reg_ler), .sel(tipo_instr));  // open: en
endmodule

module lw (
  input  [12:0] \instrução ,
  output [2:0] Reg_dest,
  output [2:0] Reg_ender
);


  assign Reg_dest = \instrução [12:10];
  assign Reg_ender = \instrução [9:7];
endmodule

module beq (
  input  [15:0] reg_entr1,
  input  [15:0] reg_entr2,
  input  [12:0] \instrução ,
  output [15:0] \saída ,
  output [2:0] Reg_1,
  output [2:0] Reg_2,
  output [2:0] Reg_dest
);

  wire undriven;

  assign \saída  = {{15{1'b0}}, undriven};  // Bit_Extender bit_extender_1

  assign Reg_1 = \instrução [9:7];
  assign Reg_2 = \instrução [6:4];
  assign Reg_dest = \instrução [12:10];
endmodule
